// Logisim project 25125027_rv32i.circ as structural Verilog: 8 circuits, main circuit processor
module ALU (
  input  [31:0] in1,
  input  [31:0] in2,
  input  [3:0] alu_control,
  output [31:0] alu_result,
  output zero_flag
);

  wire comparator_1_lt, comparator_2_lt;
  wire [31:0] adder_1_out, and_1_out, bit_extender_1_out, bit_extender_2_out, or_1_out, shifter_1_out,
       shifter_2_out, shifter_3_out, subtractor_1_out, xor_1_out;

  assign and_1_out = in1 & in2;  // AND_Gate and_1, 32 bits wide
  assign or_1_out = in1 | in2;  // OR_Gate or_1, 32 bits wide
  Adder #(.width(32)) adder_1 (.a(in1), .b(in2), .out(adder_1_out));  // open: cin, cout
  Shifter #(.width(32)) shifter_1 (.in(in1), .\dist (in2[4:0]), .out(shifter_1_out));
  Subtractor #(.width(32)) subtractor_1 (.a(in1), .b(in2), .out(subtractor_1_out));  // open: bin, bout
  Shifter #(.shift("lr"), .width(32)) shifter_2 (.in(in1), .\dist (in2[4:0]), .out(shifter_2_out));
  Shifter #(.shift("ar"), .width(32)) shifter_3 (.in(in1), .\dist (in2[4:0]), .out(shifter_3_out));
  assign xor_1_out = in1 ^ in2;  // XOR_Gate xor_1, 32 bits wide
  Comparator #(.width(32)) comparator_1 (.a(in1), .b(in2), .lt(comparator_1_lt));  // open: gt, eq
  Comparator #(.mode("unsigned"), .width(32)) comparator_2 (.a(in1), .b(in2), .lt(comparator_2_lt));  // open: gt, eq
  assign bit_extender_1_out = {{31{1'b0}}, comparator_1_lt};  // Bit_Extender bit_extender_1
  assign bit_extender_2_out = {{31{1'b0}}, comparator_2_lt};  // Bit_Extender bit_extender_2
  Multiplexer #(.select(4), .width(32)) multiplexer_1 (
    .in0(and_1_out), .in1(or_1_out), .in2(adder_1_out), .in3(shifter_1_out), .in4(subtractor_1_out),
    .in5(shifter_2_out), .in6(shifter_3_out), .in7(xor_1_out), .in8(bit_extender_1_out),
    .in9(bit_extender_2_out), .out({alu_result[31:14], alu_result[14], alu_result[12:0]}), .sel(alu_control));  // open: in10, in11, in12, in13, in14, in15
  nor nor_1 (zero_flag, alu_result[0], alu_result[1], alu_result[2], alu_result[3], alu_result[4], alu_result[5], alu_result[6], alu_result[7], alu_result[8], alu_result[9], alu_result[10], alu_result[11], alu_result[12], alu_result[14], alu_result[14], alu_result[15], alu_result[16], alu_result[17], alu_result[18], alu_result[19], alu_result[20], alu_result[21], alu_result[22], alu_result[23], alu_result[24], alu_result[25], alu_result[26], alu_result[27], alu_result[28], alu_result[29], alu_result[30], alu_result[31]);

  assign alu_result[13] = alu_result[14];

  // Notes on the sheet:
  //     0000       AND   0001       OR   0010       ADD   0011       SLL  (shift left logical)   0100       SUB   0101       SRL  (shift right logical)   0110       SRA  (shift right arithmetic)   0111       XOR   1000       SLT  (signed less-than)   1001       SLTU (unsigned less-than)
endmodule

module imm_gen (
  input  [31:0] instruction,
  output [31:0] imm_out
);

  wire comparator_1_eq, comparator_2_eq, comparator_3_eq, comparator_4_eq, comparator_5_eq, comparator_6_eq,
       comparator_7_eq, comparator_8_eq, or_1_out, or_2_out, priority_encoder_1_en_out;
  wire [2:0] select;
  wire [31:0] bit_extender_1_out, bit_extender_2_out, bit_extender_3_out, bit_extender_4_out;

  assign bit_extender_1_out = {{20{instruction[31]}}, instruction[31:20]};  // Bit_Extender bit_extender_1
  assign bit_extender_2_out = {{20{instruction[31]}}, {instruction[31:25], instruction[11:7]}};  // Bit_Extender bit_extender_2
  assign bit_extender_3_out = {{19{instruction[31]}}, {instruction[31], instruction[7], instruction[30:25], instruction[11:8], 1'b0}};  // Bit_Extender bit_extender_3
  assign bit_extender_4_out = {{11{instruction[31]}}, {instruction[31], instruction[19:12], instruction[20], instruction[30:21], 1'b0}};  // Bit_Extender bit_extender_4
  Multiplexer #(.select(3), .width(32)) multiplexer_1 (
    .in1(bit_extender_1_out), .in2(bit_extender_2_out), .in3(bit_extender_3_out),
    .in4({instruction[31:12], {12{1'b0}}}), .in5(bit_extender_4_out), .out(imm_out), .sel(select));  // open: in0, in6, in7
  Comparator #(.mode("unsigned"), .width(7)) comparator_1 (
    .a(instruction[6:0]), .b(7'b1100111), .eq(comparator_1_eq));  // open: gt, lt
  Comparator #(.width(7)) comparator_2 (.a(instruction[6:0]), .b(7'b0000011), .eq(comparator_2_eq));  // open: gt, lt
  Comparator #(.mode("unsigned"), .width(7)) comparator_3 (
    .a(instruction[6:0]), .b(7'b0010011), .eq(comparator_3_eq));  // open: gt, lt
  Comparator #(.mode("unsigned"), .width(7)) comparator_4 (
    .a(instruction[6:0]), .b(7'b0100011), .eq(comparator_4_eq));  // open: gt, lt
  Comparator #(.mode("unsigned"), .width(7)) comparator_5 (
    .a(instruction[6:0]), .b(7'b1100011), .eq(comparator_5_eq));  // open: gt, lt
  Comparator #(.mode("unsigned"), .width(7)) comparator_6 (
    .a(instruction[6:0]), .b(7'b0110111), .eq(comparator_6_eq));  // open: gt, lt
  Comparator #(.mode("unsigned"), .width(7)) comparator_7 (
    .a(instruction[6:0]), .b(7'b0010111), .eq(comparator_7_eq));  // open: gt, lt
  Comparator #(.mode("unsigned"), .width(7)) comparator_8 (
    .a(instruction[6:0]), .b(7'b1101111), .eq(comparator_8_eq));  // open: gt, lt
  or or_1 (or_1_out, comparator_1_eq, comparator_2_eq, comparator_3_eq);
  or or_2 (or_2_out, comparator_6_eq, comparator_7_eq);
  Priority_Encoder priority_encoder_1 (
    .in0(1'b0), .in1(or_1_out), .in2(comparator_4_eq), .in3(comparator_5_eq), .in4(or_2_out),
    .in5(comparator_8_eq), .out(select), .en_out(priority_encoder_1_en_out));  // open: in6, in7, en_in, gs
  // also tied to VCC on the sheet: priority_encoder_1_en_out

  // Other names for the same wires on the sheet: OPCODE[6:0] = instruction[6:0]; B_mid = instruction[7];
  //   S_lo[4:0] = instruction[11:7]; B_lo[3:0] = instruction[11:8]; J_mid[7:0] = instruction[19:12];
  //   U_imm[19:0] = instruction[31:12]; I_imm[11:0] = instruction[31:20]; J_bit20 = instruction[20];
  //   J_lo[9:0] = instruction[30:21]; S_hi[6:0] = instruction[31:25]; SB_hi[5:0] = instruction[30:25];
  //   SIGN = instruction[31]
endmodule

module reg_file (
  input  regwrite,
  input  [4:0] write_reg,
  input  [31:0] write_data,
  input  [4:0] read_reg_num1,
  input  clock,
  input  reset,
  input  [4:0] read_reg_num2,
  output [31:0] read_data1,
  output [31:0] read_data2
);

  wire and_1_out, and_2_out, and_3_out, and_4_out, and_5_out, and_6_out, and_7_out, and_8_out, and_9_out,
       and_10_out, and_11_out, and_12_out, and_13_out, and_14_out, and_15_out, and_16_out, and_17_out,
       and_18_out, and_19_out, and_20_out, and_21_out, and_22_out, and_23_out, and_24_out, and_25_out,
       and_26_out, and_27_out, and_28_out, and_29_out, and_30_out, and_31_out, and_32_out, decoder_1_out0,
       decoder_1_out1, decoder_1_out2, decoder_1_out3, decoder_1_out4, decoder_1_out5, decoder_1_out6,
       decoder_1_out7, decoder_1_out8, decoder_1_out9, decoder_1_out10, decoder_1_out11, decoder_1_out12,
       decoder_1_out13, decoder_1_out14, decoder_1_out15, decoder_1_out16, decoder_1_out17, decoder_1_out18,
       decoder_1_out19, decoder_1_out20, decoder_1_out21, decoder_1_out22, decoder_1_out23, decoder_1_out24,
       decoder_1_out25, decoder_1_out26, decoder_1_out27, decoder_1_out28, decoder_1_out29, decoder_1_out30,
       decoder_1_out31;
  wire [31:0] x0, x1, x2, x3, x4, x5, x6, x7, x8, x9, x10, x11, x12, x13, x14, x15, x16, x17, x18, x19, x20,
       x21, x22, x23, x24, x25, x26, x27, x28, x29, x30, x31;

  Decoder #(.enable("false"), .select(5)) decoder_1 (
    .out0(decoder_1_out0), .out1(decoder_1_out1), .out2(decoder_1_out2), .out3(decoder_1_out3),
    .out4(decoder_1_out4), .out5(decoder_1_out5), .out6(decoder_1_out6), .out7(decoder_1_out7),
    .out8(decoder_1_out8), .out9(decoder_1_out9), .out10(decoder_1_out10), .out11(decoder_1_out11),
    .out12(decoder_1_out12), .out13(decoder_1_out13), .out14(decoder_1_out14), .out15(decoder_1_out15),
    .out16(decoder_1_out16), .out17(decoder_1_out17), .out18(decoder_1_out18), .out19(decoder_1_out19),
    .out20(decoder_1_out20), .out21(decoder_1_out21), .out22(decoder_1_out22), .out23(decoder_1_out23),
    .out24(decoder_1_out24), .out25(decoder_1_out25), .out26(decoder_1_out26), .out27(decoder_1_out27),
    .out28(decoder_1_out28), .out29(decoder_1_out29), .out30(decoder_1_out30), .out31(decoder_1_out31),
    .sel(write_reg));
  and and_1 (and_1_out, decoder_1_out31, regwrite);
  and and_2 (and_2_out, decoder_1_out30, regwrite);
  Register #(.width(32)) register_1 (.D(write_data), .en(and_1_out), .clk(clock), .Q(x31), .clr(reset));
  Register #(.width(32)) register_2 (.D(write_data), .en(and_2_out), .clk(clock), .Q(x30), .clr(reset));
  Register #(.width(32)) register_3 (.D(write_data), .en(and_3_out), .clk(clock), .Q(x29), .clr(reset));
  Register #(.width(32)) register_4 (.D(write_data), .en(and_4_out), .clk(clock), .Q(x28), .clr(reset));
  and and_3 (and_3_out, decoder_1_out29, regwrite);
  and and_4 (and_4_out, decoder_1_out28, regwrite);
  and and_5 (and_5_out, decoder_1_out27, regwrite);
  and and_6 (and_6_out, decoder_1_out26, regwrite);
  and and_7 (and_7_out, decoder_1_out25, regwrite);
  and and_8 (and_8_out, decoder_1_out24, regwrite);
  Register #(.width(32)) register_5 (.D(write_data), .en(and_8_out), .clk(clock), .Q(x24), .clr(reset));
  Register #(.width(32)) register_6 (.D(write_data), .en(and_7_out), .clk(clock), .Q(x25), .clr(reset));
  Register #(.width(32)) register_7 (.D(write_data), .en(and_6_out), .clk(clock), .Q(x26), .clr(reset));
  Register #(.width(32)) register_8 (.D(write_data), .en(and_5_out), .clk(clock), .Q(x27), .clr(reset));
  and and_9 (and_9_out, decoder_1_out23, regwrite);
  and and_10 (and_10_out, decoder_1_out22, regwrite);
  and and_11 (and_11_out, decoder_1_out21, regwrite);
  and and_12 (and_12_out, decoder_1_out20, regwrite);
  and and_13 (and_13_out, decoder_1_out19, regwrite);
  Register #(.width(32)) register_9 (.D(write_data), .en(and_12_out), .clk(clock), .Q(x20), .clr(reset));
  Register #(.width(32)) register_10 (.D(write_data), .en(and_11_out), .clk(clock), .Q(x21), .clr(reset));
  Register #(.width(32)) register_11 (.D(write_data), .en(and_10_out), .clk(clock), .Q(x22), .clr(reset));
  Register #(.width(32)) register_12 (.D(write_data), .en(and_9_out), .clk(clock), .Q(x23), .clr(reset));
  and and_14 (and_14_out, decoder_1_out17, regwrite);
  and and_15 (and_15_out, decoder_1_out16, regwrite);
  and and_16 (and_16_out, decoder_1_out18, regwrite);
  Register #(.width(32)) register_13 (.D(write_data), .en(and_15_out), .clk(clock), .Q(x16), .clr(reset));
  Register #(.width(32)) register_14 (.D(write_data), .en(and_14_out), .clk(clock), .Q(x17), .clr(reset));
  Register #(.width(32)) register_15 (.D(write_data), .en(and_16_out), .clk(clock), .Q(x18), .clr(reset));
  Register #(.width(32)) register_16 (.D(write_data), .en(and_13_out), .clk(clock), .Q(x19), .clr(reset));
  and and_17 (and_17_out, decoder_1_out15, regwrite);
  and and_18 (and_18_out, decoder_1_out14, regwrite);
  and and_19 (and_19_out, decoder_1_out13, regwrite);
  and and_20 (and_20_out, decoder_1_out12, regwrite);
  and and_21 (and_21_out, decoder_1_out11, regwrite);
  Register #(.width(32)) register_17 (.D(write_data), .en(and_20_out), .clk(clock), .Q(x12), .clr(reset));
  Register #(.width(32)) register_18 (.D(write_data), .en(and_19_out), .clk(clock), .Q(x13), .clr(reset));
  Register #(.width(32)) register_19 (.D(write_data), .en(and_18_out), .clk(clock), .Q(x14), .clr(reset));
  Register #(.width(32)) register_20 (.D(write_data), .en(and_17_out), .clk(clock), .Q(x15), .clr(reset));
  and and_22 (and_22_out, decoder_1_out10, regwrite);
  and and_23 (and_23_out, decoder_1_out9, regwrite);
  and and_24 (and_24_out, decoder_1_out8, regwrite);
  and and_25 (and_25_out, decoder_1_out7, regwrite);
  and and_26 (and_26_out, decoder_1_out6, regwrite);
  Register #(.width(32)) register_21 (.D(write_data), .en(and_24_out), .clk(clock), .Q(x8), .clr(reset));
  Register #(.width(32)) register_22 (.D(write_data), .en(and_23_out), .clk(clock), .Q(x9), .clr(reset));
  Register #(.width(32)) register_23 (.D(write_data), .en(and_22_out), .clk(clock), .Q(x10), .clr(reset));
  Register #(.width(32)) register_24 (.D(write_data), .en(and_21_out), .clk(clock), .Q(x11), .clr(reset));
  and and_27 (and_27_out, decoder_1_out5, regwrite);
  and and_28 (and_28_out, decoder_1_out4, regwrite);
  and and_29 (and_29_out, decoder_1_out3, regwrite);
  Register #(.width(32)) register_25 (.D(write_data), .en(and_28_out), .clk(clock), .Q(x4), .clr(reset));
  Register #(.width(32)) register_26 (.D(write_data), .en(and_27_out), .clk(clock), .Q(x5), .clr(reset));
  Register #(.width(32)) register_27 (.D(write_data), .en(and_26_out), .clk(clock), .Q(x6), .clr(reset));
  Register #(.width(32)) register_28 (.D(write_data), .en(and_25_out), .clk(clock), .Q(x7), .clr(reset));
  and and_30 (and_30_out, decoder_1_out2, regwrite);
  and and_31 (and_31_out, decoder_1_out1, regwrite);
  and and_32 (and_32_out, decoder_1_out0, 1'b0);
  Register #(.width(32)) register_29 (.D(write_data), .en(and_32_out), .clk(clock), .Q(x0), .clr(reset));
  Register #(.width(32)) register_30 (.D(write_data), .en(and_31_out), .clk(clock), .Q(x1), .clr(reset));
  Register #(.width(32)) register_31 (.D(write_data), .en(and_30_out), .clk(clock), .Q(x2), .clr(reset));
  Register #(.width(32)) register_32 (.D(write_data), .en(and_29_out), .clk(clock), .Q(x3), .clr(reset));
  Multiplexer #(.enable("true"), .select(5), .width(32)) multiplexer_1 (
    .in0(x0), .in1(x1), .in2(x2), .in3(x3), .in4(x4), .in5(x5), .in6(x6), .in7(x7), .in8(x8), .in9(x9),
    .in10(x10), .in11(x11), .in12(x12), .in13(x13), .in14(x14), .in15(x15), .in16(x16), .in17(x17),
    .in18(x18), .in19(x19), .in20(x20), .in21(x21), .in22(x22), .in23(x23), .in24(x24), .in25(x25),
    .in26(x26), .in27(x27), .in28(x28), .in29(x29), .in30(x30), .in31(x31), .out(read_data1),
    .sel(read_reg_num1));  // open: en
  Multiplexer #(.select(5), .width(32)) multiplexer_2 (
    .in0(x0), .in1(x1), .in2(x2), .in3(x3), .in4(x4), .in5(x5), .in6(x6), .in7(x7), .in8(x8), .in9(x9),
    .in10(x10), .in11(x11), .in12(x12), .in13(x13), .in14(x14), .in15(x15), .in16(x16), .in17(x17),
    .in18(x18), .in19(x19), .in20(x20), .in21(x21), .in22(x22), .in23(x23), .in24(x24), .in25(x25),
    .in26(x26), .in27(x27), .in28(x28), .in29(x29), .in30(x30), .in31(x31), .out(read_data2),
    .sel(read_reg_num2));

  // Other names for the same wires on the sheet: clkp = clock; rp = reset; wdp[31:0] = write_data
endmodule

module control_unit (
  input  [6:0] opcode,
  input  [2:0] funct3,
  input  funct7,
  output regwrite,
  output [3:0] alu_control,
  output mem_write,
  output lui,
  output auipc,
  output jalr,
  output jump,
  output branch,
  output alu_src,
  output [1:0] mem_to_reg,
  output mem_read
);

  wire [0:0] rom_1_data;

  ROM #(.addrWidth(11), .dataWidth(16)) rom_1 (
    .addr({opcode, funct3, funct7}),
    .data({alu_control, alu_src, regwrite, mem_read, mem_write, mem_to_reg, branch, jump, jalr, auipc, lui, rom_1_data[0]}));

  // Notes on the sheet:
  //   contents of rom_1 (hex, n*v repeats v):
  //   48*0 2e40 0 2e40 0 2e40 0 0 0 2e40 0 2e40 245*0 2c00 0 3c00 0 8c00 0 9c00 0 7c00 0 5c00 6c00 1c00 0
  //   c00 49*0 2c04 191*0 2900 0 2900 0 2900 251*0 2400 4400 3400 0 8400 0 9400 0 7400 0 5400 6400 1400 0
  //   400 49*0 2402 703*0 4020 0 4020 5*0 8020 0 8020 0 9020 0 9020 49*0 2c98 127*0 2490
endmodule

module branch_extractor (
  input  [31:0] alu_result,
  input  zero_flag,
  input  [2:0] funct3,
  output branch_taken
);

  wire not_1_out;

  not not_1 (not_1_out, alu_result[0]);
  Multiplexer #(.select(3)) multiplexer_1 (
    .in0(zero_flag), .in1(zero_flag), .in2(1'b0), .in3(1'b0), .in4(alu_result[0]), .in5(not_1_out),
    .in6(alu_result[0]), .in7(not_1_out), .out(branch_taken), .sel(funct3));
endmodule

module store_unit (
  input  [31:0] rs2_data,
  input  [2:0] funct3,
  input  [1:0] byte_offset,
  output [31:0] store_data,
  output [3:0] store_mask
);

  wire [3:0] decoder_1_out0, multiplexer_1_out;

  Multiplexer #(.width(4)) multiplexer_1 (.in0(4'b0011), .in1(4'b1100), .out(multiplexer_1_out), .sel(byte_offset[1]));
  Decoder #(.enable("false"), .select(2)) decoder_1 (
    .out0(decoder_1_out0[0]), .out1(decoder_1_out0[1]), .out2(decoder_1_out0[2]), .out3(decoder_1_out0[3]),
    .sel(byte_offset));
  Multiplexer #(.select(3), .width(32)) multiplexer_2 (
    .in0({rs2_data[7:0], rs2_data[7:0], rs2_data[7:0], rs2_data[7:0]}),
    .in1({rs2_data[15:0], rs2_data[15:0]}), .in2(rs2_data), .out(store_data), .sel(funct3));  // open: in3, in4, in5, in6, in7
  Multiplexer #(.select(3), .width(4)) multiplexer_3 (
    .in0(decoder_1_out0), .in1(multiplexer_1_out), .in2(4'b1111), .in3(4'b0000), .out(store_mask),
    .sel(funct3));  // open: in4, in5, in6, in7
endmodule

module load_extractor (
  input  [31:0] raw_data,
  input  [1:0] byte_offset,
  input  [2:0] funct3,
  output [31:0] load_data
);

  wire [7:0] multiplexer_1_out;
  wire [15:0] multiplexer_2_out;
  wire [31:0] bit_extender_1_out, bit_extender_2_out, bit_extender_3_out, bit_extender_4_out;

  Multiplexer #(.select(2), .width(8)) multiplexer_1 (
    .in0(raw_data[7:0]), .in1(raw_data[15:8]), .in2(raw_data[23:16]), .in3(raw_data[31:24]),
    .out(multiplexer_1_out), .sel(byte_offset));
  Multiplexer #(.width(16)) multiplexer_2 (
    .in0(raw_data[15:0]), .in1(raw_data[31:16]), .out(multiplexer_2_out), .sel(byte_offset[1]));
  assign bit_extender_1_out = {{24{multiplexer_1_out[7]}}, multiplexer_1_out};  // Bit_Extender bit_extender_1
  assign bit_extender_2_out = {{24{1'b0}}, multiplexer_1_out};  // Bit_Extender bit_extender_2
  assign bit_extender_3_out = {{16{multiplexer_2_out[15]}}, multiplexer_2_out};  // Bit_Extender bit_extender_3
  assign bit_extender_4_out = {{16{1'b0}}, multiplexer_2_out};  // Bit_Extender bit_extender_4
  Multiplexer #(.select(3), .width(32)) multiplexer_3 (
    .in0(bit_extender_1_out), .in1(bit_extender_3_out), .in2(raw_data), .in3({32{1'b0}}),
    .in4(bit_extender_2_out), .in5(bit_extender_4_out), .out(load_data), .sel(funct3));  // open: in6, in7
endmodule

module processor (
  input  mem_rbusy,
  input  mem_wbusy,
  input  reset,
  output mem_rstrb
);

  wire alu_1_zero_flag, and_1_out, and_2_out, and_3_out, and_4_out, and_5_out, and_6_out, and_7_out,
       and_8_out, and_10_out, and_11_out, and_12_out, branch_extractor_1_branch_taken, clkp, comparator_1_eq,
       comparator_2_eq, comparator_3_eq, comparator_6_eq, comparator_7_eq, comparator_8_eq, comparator_9_eq,
       control_unit_1_alu_src, control_unit_1_auipc, control_unit_1_branch, control_unit_1_jalr,
       control_unit_1_jump, control_unit_1_lui, control_unit_1_mem_read, control_unit_1_mem_write,
       control_unit_1_regwrite, FSM_q, is_exec, is_fetch, not_1_out, not_2_out, not_3_out, not_4_out,
       not_5_out, not_6_out, not_7_out, or_2_out, or_3_out, or_4_out, or_6_out, stall;
  wire [1:0] control_unit_1_mem_to_reg;
  wire [2:0] funct3, instr_reg_q;
  wire [3:0] control_unit_1_alu_control, mem_wmask, store_mask;
  wire [4:0] rd, rs1, rs2;
  wire [6:0] funct7, instr_reg_q_2, opcode;
  wire [31:0] adder_1_out, adder_2_out, alu_result, and_9_out, imm_out, instructions_data,
       load_extractor_1_load_data, mem_addr, mem_rdata, mem_wdata, multiplexer_5_out, multiplexer_6_out,
       multiplexer_7_out, multiplexer_8_out, multiplexer_10_out, next_pc, old_pc, PC, reg_file_1_read_data1,
       reg_file_1_read_data2, write_back_data;

  Clock clk (.out(clkp));
  not not_1 (not_1_out, stall);
  and and_1 (and_1_out, not_1_out, is_exec);
  not not_2 (not_2_out, stall);
  ROM #(.addrWidth(10), .dataWidth(32)) instructions (.addr(PC[11:2]), .data(instructions_data));
  Register #(.width(32)) pc_reg (.D(next_pc), .en(and_1_out), .clk(clkp), .Q(PC), .clr(reset));
  Register #(.width(1)) FSM (.D(not_3_out), .en(not_2_out), .clk(clkp), .Q(FSM_q), .clr(reset));
  not not_3 (not_3_out, FSM_q);
  Adder #(.width(32)) adder_1 (.a(PC), .b(32'h4), .out(adder_1_out));  // open: cin, cout
  Comparator #(.width(7)) comparator_1 (.a(7'b0110111), .b(opcode), .eq(comparator_1_eq));  // open: gt, lt
  Comparator #(.width(7)) comparator_2 (.a(opcode), .b(7'b0010111), .eq(comparator_2_eq));  // open: gt, lt
  Comparator #(.width(7)) comparator_3 (.a(opcode), .b(7'b1101111), .eq(comparator_3_eq));  // open: gt, lt
  Register #(.width(32)) instr_reg (
    .D(instructions_data), .en(not_4_out), .clk(clkp),
    .Q({instr_reg_q_2, rs2, rs1, instr_reg_q, rd, opcode}), .clr(reset));
  not not_4 (not_4_out, stall);
  or or_1 (mem_rstrb, is_fetch, and_2_out);
  Subtractor #(.width(32)) subtractor_1 (.a(PC), .b(32'h4), .out(old_pc));  // open: bin, bout
  Multiplexer #(.width(3)) multiplexer_1 (.in0(instr_reg_q), .in1(3'b000), .out(funct3), .sel(or_2_out));
  or or_2 (or_2_out, comparator_1_eq, comparator_3_eq, comparator_2_eq);
  and and_2 (and_2_out, is_exec, control_unit_1_mem_read);
  Comparator #(.width(1)) comparator_4 (.a(FSM_q), .b(1'b0), .eq(is_fetch));  // open: gt, lt
  Comparator #(.width(1)) comparator_5 (.a(FSM_q), .b(1'b1), .eq(is_exec));  // open: gt, lt
  and and_3 (and_3_out, control_unit_1_regwrite, is_exec, not_5_out);
  Multiplexer #(.width(4)) multiplexer_2 (.in0(4'b0000), .in1(store_mask), .out(mem_wmask), .sel(and_4_out));
  or or_3 (or_3_out, and_6_out, comparator_9_eq);
  Multiplexer #(.width(7)) multiplexer_3 (.in0({7{1'b0}}), .in1(instr_reg_q_2), .out(funct7), .sel(or_3_out));
  Comparator #(.width(7)) comparator_6 (.a(opcode), .b(7'b0010011), .eq(comparator_6_eq));  // open: gt, lt
  not not_5 (not_5_out, stall);
  Multiplexer #(.width(32)) multiplexer_4 (.in0(alu_result), .in1(PC), .out(mem_addr), .sel(is_fetch));
  and and_4 (and_4_out, is_exec, control_unit_1_mem_write);
  imm_gen imm_gen_1 (.instruction({instr_reg_q_2, rs2, rs1, instr_reg_q, rd, opcode}), .imm_out(imm_out));
  Comparator #(.width(3)) comparator_7 (.a(funct3), .b(3'b101), .eq(comparator_7_eq));  // open: gt, lt
  Comparator #(.width(3)) comparator_8 (.a(funct3), .b(3'b001), .eq(comparator_8_eq));  // open: gt, lt
  and and_5 (and_5_out, is_fetch, mem_rbusy);
  and and_6 (and_6_out, comparator_6_eq, or_4_out);
  or or_4 (or_4_out, comparator_7_eq, comparator_8_eq);
  reg_file reg_file_1 (
    .regwrite(and_3_out), .write_reg(rd), .write_data(write_back_data), .read_reg_num1(rs1), .clock(clkp),
    .reset(reset), .read_reg_num2(rs2), .read_data1(reg_file_1_read_data1), .read_data2(reg_file_1_read_data2));
  control_unit control_unit_1 (
    .opcode(opcode), .funct3(funct3), .funct7(funct7[5]), .regwrite(control_unit_1_regwrite),
    .alu_control(control_unit_1_alu_control), .mem_write(control_unit_1_mem_write), .lui(control_unit_1_lui),
    .auipc(control_unit_1_auipc), .jalr(control_unit_1_jalr), .jump(control_unit_1_jump),
    .branch(control_unit_1_branch), .alu_src(control_unit_1_alu_src), .mem_to_reg(control_unit_1_mem_to_reg),
    .mem_read(control_unit_1_mem_read));
  and and_7 (and_7_out, mem_rbusy, is_exec, control_unit_1_mem_read);
  and and_8 (and_8_out, is_exec, control_unit_1_mem_write, mem_wbusy);
  Comparator #(.width(7)) comparator_9 (.a(7'b0110011), .b(opcode), .eq(comparator_9_eq));  // open: gt, lt
  Multiplexer #(.width(32)) multiplexer_5 (
    .in0(reg_file_1_read_data1), .in1(PC), .out(multiplexer_5_out), .sel(control_unit_1_auipc));
  Multiplexer #(.width(32)) multiplexer_6 (
    .in0(reg_file_1_read_data2), .in1(imm_out), .out(multiplexer_6_out), .sel(control_unit_1_alu_src));
  or or_5 (stall, and_5_out, and_7_out, and_8_out);
  assign and_9_out = alu_result & 32'hfffffffe;  // AND_Gate and_9, 32 bits wide
  ALU alu_1 (
    .in1(multiplexer_5_out), .in2(multiplexer_6_out), .alu_control(control_unit_1_alu_control),
    .alu_result(alu_result), .zero_flag(alu_1_zero_flag));
  and and_10 (and_10_out, control_unit_1_jalr, control_unit_1_jump);
  Adder #(.width(32)) adder_2 (.a(imm_out), .b(PC), .out(adder_2_out));  // open: cin, cout
  Multiplexer #(.width(32)) multiplexer_7 (
    .in0(adder_1_out), .in1(adder_2_out), .out(multiplexer_7_out), .sel(and_11_out));
  and and_11 (and_11_out, branch_extractor_1_branch_taken, control_unit_1_branch);
  branch_extractor branch_extractor_1 (
    .alu_result(alu_result), .zero_flag(alu_1_zero_flag), .funct3(funct3),
    .branch_taken(branch_extractor_1_branch_taken));
  store_unit store_unit_1 (
    .rs2_data(reg_file_1_read_data2), .funct3(funct3), .byte_offset(alu_result[1:0]), .store_data(mem_wdata),
    .store_mask(store_mask));
  load_extractor load_extractor_1 (
    .raw_data(mem_rdata), .byte_offset(alu_result[1:0]), .funct3(funct3),
    .load_data(load_extractor_1_load_data));
  Multiplexer #(.width(32)) multiplexer_8 (
    .in0(multiplexer_7_out), .in1(adder_2_out), .out(multiplexer_8_out), .sel(control_unit_1_jump));
  not not_6 (not_6_out, mem_wbusy);
  Multiplexer #(.width(32)) multiplexer_9 (.in0(multiplexer_8_out), .in1(and_9_out), .out(next_pc), .sel(and_10_out));
  and and_12 (and_12_out, or_6_out, not_6_out);
  Multiplexer #(.select(2), .width(32)) multiplexer_10 (
    .in0(alu_result), .in1(load_extractor_1_load_data), .in2(adder_1_out), .in3(imm_out),
    .out(multiplexer_10_out), .sel(control_unit_1_mem_to_reg));
  not not_7 (not_7_out, mem_rbusy);
  Multiplexer #(.width(32)) multiplexer_11 (
    .in0(multiplexer_10_out), .in1(imm_out), .out(write_back_data), .sel(control_unit_1_lui));
  or or_6 (or_6_out, mem_wmask[0], mem_wmask[1], mem_wmask[2], mem_wmask[3]);
  RAM #(.addrWidth(10), .asyncread("true"), .byteenables("byteEnables"), .dataWidth(32)) memory (
    .addr(mem_addr[11:2]), .we(and_12_out), .oe(not_7_out), .clk(clkp), .din(mem_wdata), .dout(mem_rdata),
    .be3(mem_wmask[3]), .be2(mem_wmask[2]), .be1(mem_wmask[1]), .be0(mem_wmask[0]));

  // Other names for the same wires on the sheet: byte_offset[1:0] = alu_result[1:0]; clr = reset

  // Notes on the sheet:
  //   srli and srai
  //   started: 12th April
  //   finished: 18th April
  //   rv 32i processor
  //   Put the clock on  when reset 0->1->0
  //   then do clock ticks to run through the instructions
  //   It is a 2 cycle, fetch state and execute state, processor
  //   funct3 for jal, lui and auipc are dont care
  //   All the instructions that were provided, in the verilog
  //   assignment are ran and checked manually
  //   So, if any instruction doesn't works do contact
  //   cycle 1
  //   tick 1: on -> off
  //   tick 2: off -> on
  //   cycle 2
  //   tick 3: on -> off
  //   tick 4: off -> on
  //   set to 1 to reset the processor
  //   then set to 0 again
  //   similarly funct7 we only care about funct7 in Rtype and slli
  //   This processor is implemented totally by reading the docs
  //   provided in the help menu on top left, following my verilog
  //   contents of instructions (hex, n*v repeats v):
  //   500093 300113 2081b3 40208233 ff000293 4022d333 22d3b3 100056f 700713 800793 900813 100593 3700613
  //   506e7 6300a93 6300a93 0 0 0 6300813 200813 116463 6300893 300893 20f463 6300913 400913 13
endmodule
